# Fritzing sketch Eclairage_Auto (saved by Fritzing 0.9.2b)
breadboards: 1

parts:
  Composant1 = Arduino Uno (Rev3)
  R1 = Resistor [tolerance=±5% resistance=220 package=THT]  # not connected
  R2 = Photocell (LDR) [package=THT]
  KY-1 = Keyes Relay [package=THT]
  LED1 = LEDs [package=led10mm]
  Power_plug1 = Power plug

nets:
  N1: Composant1.A0, R2.pin_0
  N2: Composant1.D3_PWM, KY-1.signal
  N3: Composant1.5V, R2.pin_1, KY-1.power
  N4: Composant1.GND, KY-1.ground
  N5: KY-1.C, Power_plug1.VCC
  N6: KY-1.NO, LED1.C
  N7: LED1.A, Power_plug1.GND

custom parts:
  Keyes Relay: The Keyes 5V relay module is suitable for SCM development, home appliance control. It uses a 5V~12V TIL control signal which can control DC / AC signal.
